// Logisim project singleCycleProcessorMIPS.circ as structural Verilog: 8 circuits, main circuit main
module main (
  input  RESET
);

  wire ALUsrc, BEQ, BGEZ, BGTZ, BLEZ, BLTZ, BNE, branchunit_1_branch, carryFlag, CLK, JUMP, MemRead,
       MemtoReg, MemWrite, negativeFlag, overflowFlag, RegWrite, SLTtype, zeroFlag;
  wire [1:0] MemWriteSize, offset, shiftControl;
  wire [2:0] MemReadType;
  wire [3:0] ALUcontrol;
  wire [4:0] RegA_read, RegB_read, RegC_write;
  wire [5:0] Func, OpCode;
  wire [15:6] Imm16;
  wire [23:0] MemAddress;
  wire [25:16] Imm26;
  wire [31:0] Imm32, multiplexer_1_out, multiplexer_2_out, programcounter_1_pc, RB, RC,
       registerfile_1_rega_data;
  wire [31:26] alu_1_c;

  BranchUnit branchunit_1 (
    .negativeFlag(negativeFlag), .zeroFlag(zeroFlag), .BEQ(BEQ), .BNE(BNE), .BLTZ(BLTZ), .BLEZ(BLEZ),
    .BGTZ(BGTZ), .BGEZ(BGEZ), .BRANCH(branchunit_1_branch));
  ProgramCounter programcounter_1 (
    .Imm32(Imm32), .RESET(RESET), .JUMP(JUMP), .BRANCH(branchunit_1_branch), .PC(programcounter_1_pc));
  MemInstructions meminstructions_1 (.PC(programcounter_1_pc[13:2]), .Instruction({OpCode, Imm26, Imm16, Func}));
  Multiplexer #(.width(32)) multiplexer_1 (
    .in0({alu_1_c, MemAddress, offset}), .in1(RC), .out(multiplexer_1_out), .sel(MemtoReg));
  Clock u_CLK (.out(CLK));
  RegisterFile registerfile_1 (
    .CLK(CLK), .RegC_Data(multiplexer_1_out), .RegWrite(RegWrite), .RegC_write(RegC_write),
    .RegA_read(RegA_read), .RegB_read(RegB_read), .RegA_Data(registerfile_1_rega_data), .RegB_Data(RB));
  Multiplexer #(.width(32)) multiplexer_2 (.in0(RB), .in1(Imm32), .out(multiplexer_2_out), .sel(ALUsrc));
  ControlUnit controlunit_1 (
    .Opcode(OpCode), .Rs(Imm26[25:21]), .Rt(Imm26[20:16]), .Rd(Imm16[15:11]), .sa(Imm16[10:6]), .func(Func),
    .imm16({Imm16, Func}), .imm26({Imm26, Imm16, Func}), .RA(RegA_read), .RB(RegB_read), .RC(RegC_write),
    .Imm32(Imm32), .SLTtype(SLTtype), .MemtoReg(MemtoReg), .ALUsrc(ALUsrc), .MemRead(MemRead),
    .RegWrite(RegWrite), .MemWrite(MemWrite), .MemWriteSize(MemWriteSize), .MemReadType(MemReadType),
    .ALUcontrol(ALUcontrol), .JUMP(JUMP), .ShiftControl(shiftControl), .BEQ(BEQ), .BNE(BNE), .BLEZ(BLEZ),
    .BGTZ(BGTZ), .BLTZ(BLTZ), .BGEZ(BGEZ));
  ALU alu_1 (
    .A(registerfile_1_rega_data), .B(multiplexer_2_out), .ALUcontrol(ALUcontrol), .shamt(Imm16[10:6]),
    .shiftControl(shiftControl), .SLTtype(SLTtype), .C({alu_1_c, MemAddress, offset}), .carryFlag(carryFlag),
    .overflowFlag(overflowFlag), .negativeFlag(negativeFlag), .zeroFlag(zeroFlag));
  MemData memdata_1 (
    .StoreData(RB), .offset(offset), .RAMaddress(MemAddress), .MemWrite(MemWrite), .MemRead(MemRead),
    .CLK(CLK), .MemWriteSize(MemWriteSize), .MemReadType(MemReadType), .LoadData(RC));

  // Other names for the same wires on the sheet: Imm16[5:0] = Func; Imm26[15:0] = {Imm16, Func};
  //   shamt[4:0] = Imm16[10:6]; Rd[4:0] = Imm16[15:11]; Rt[4:0] = Imm26[20:16]; Rs[4:0] = Imm26[25:21]
endmodule

module ALU (
  input  [31:0] A,
  input  [31:0] B,
  input  [3:0] ALUcontrol,
  input  [4:0] shamt,
  input  [1:0] shiftControl,
  input  SLTtype,
  output [31:0] C,
  output carryFlag,
  output overflowFlag,
  output negativeFlag,
  output zeroFlag
);

  wire and_2_out, and_3_out, not_2_out, not_3_out, not_4_out, not_5_out, xor_2_out;
  wire [4:0] shiftVal;
  wire [31:0] adderRESULT, and_1_out, bit_extender_1_out, bit_extender_2_out, BofAdder, multiplexer_2_out,
       nor_1_out, not_1_out, or_1_out, shifter_1_out, shifter_2_out, shifter_3_out, xor_1_out;

  assign not_1_out = ~B;  // NOT_Gate not_1, 32 bits wide
  Multiplexer #(.width(32)) multiplexer_1 (.in0(B), .in1(not_1_out), .out(BofAdder), .sel(ALUcontrol[0]));
  not not_2 (not_2_out, carryFlag);
  Adder #(.width(32)) adder_1 (.a(A), .b(BofAdder), .out(adderRESULT), .cin(ALUcontrol[0]), .cout(carryFlag));
  not not_3 (not_3_out, A[31]);
  assign and_1_out = A & B;  // AND_Gate and_1, 32 bits wide
  assign or_1_out = A | B;  // OR_Gate or_1, 32 bits wide
  assign nor_1_out = ~(A | B);  // NOR_Gate nor_1, 32 bits wide
  assign xor_1_out = A ^ B;  // XOR_Gate xor_1, 32 bits wide
  xor xor_2 (xor_2_out, adderRESULT[31], overflowFlag);
  not not_4 (not_4_out, BofAdder[31]);
  not not_5 (not_5_out, adderRESULT[31]);
  nor nor_2 (zeroFlag, C[31], C[30], C[29], C[28], C[27], C[26], C[25], C[24], C[23], C[22], C[21], C[20], C[19], C[18], C[17], C[16], C[15], C[14], C[13], C[12], C[11], C[10], C[9], C[8], C[7], C[6], C[5], C[4], C[3], C[2], C[1], C[0]);
  assign bit_extender_1_out = {{31{1'b0}}, xor_2_out};  // Bit_Extender bit_extender_1
  assign bit_extender_2_out = {{31{1'b0}}, not_2_out};  // Bit_Extender bit_extender_2
  Multiplexer #(.width(32)) multiplexer_2 (
    .in0(bit_extender_1_out), .in1(bit_extender_2_out), .out(multiplexer_2_out), .sel(SLTtype));
  and and_2 (and_2_out, not_3_out, adderRESULT[31], not_4_out);
  and and_3 (and_3_out, A[31], BofAdder[31], not_5_out);
  Shifter #(.width(32)) shifter_1 (.in(B), .\dist (shiftVal), .out(shifter_1_out));
  Shifter #(.shift("lr"), .width(32)) shifter_2 (.in(B), .\dist (shiftVal), .out(shifter_2_out));
  Shifter #(.shift("ar"), .width(32)) shifter_3 (.in(B), .\dist (shiftVal), .out(shifter_3_out));
  or or_2 (overflowFlag, and_2_out, and_3_out);
  Multiplexer #(.select(4), .width(32)) multiplexer_3 (
    .in0(adderRESULT), .in1(adderRESULT), .in2(and_1_out), .in3(or_1_out), .in4(nor_1_out),
    .in5(multiplexer_2_out), .in6(xor_1_out), .in7(shifter_1_out), .in8(shifter_2_out), .in9(shifter_3_out),
    .in10({32{1'b0}}), .in11({32{1'b0}}), .in12({32{1'b0}}), .in13({32{1'b0}}), .in14({32{1'b0}}),
    .in15({32{1'b0}}), .out(C), .sel(ALUcontrol));
  Multiplexer #(.select(2), .width(5)) multiplexer_4 (
    .in0(shamt), .in1(A[4:0]), .in2(5'b10000), .in3({5{1'b0}}), .out(shiftVal), .sel(shiftControl));

  assign negativeFlag = A[31];

  // Other names for the same wires on the sheet: ADD0SUB1 = ALUcontrol[0]; Co = carryFlag

  // Notes on the sheet:
  //   ADD 0000, SUB 0001, AND 0010, OR 0011, NOR 0100, SLT 0101, XOR 0110, SLL 0111, SRL 1000, SRA 1001
endmodule

module RegisterFile (
  input  CLK,
  input  [31:0] RegC_Data,
  input  RegWrite,
  input  [4:0] RegC_write,
  input  [4:0] RegA_read,
  input  [4:0] RegB_read,
  output [31:0] RegA_Data,
  output [31:0] RegB_Data
);

  wire WE0, WE1, WE2, WE3, WE4, WE5, WE6, WE7, WE8, WE9, WE10, WE11, WE12, WE13, WE14, WE15, WE16, WE17,
       WE18, WE19, WE20, WE21, WE22, WE23, WE24, WE25, WE26, WE27, WE28, WE29, WE30, WE31;
  wire [31:0] Reg0_out, Reg1_out, Reg2_out, Reg3_out, Reg4_out, Reg5_out, Reg6_out, Reg7_out, Reg8_out,
       Reg9_out, Reg10_out, Reg11_out, Reg12_out, Reg13_out, Reg14_out, Reg15_out, Reg16_out, Reg17_out,
       Reg18_out, Reg19_out, Reg20_out, Reg21_out, Reg22_out, Reg23_out, Reg24_out, Reg25_out, Reg26_out,
       Reg27_out, Reg28_out, Reg29_out, Reg30_out, Reg31_out;

  Demultiplexer #(.select(5)) demultiplexer_1 (
    .out0(WE0), .out1(WE1), .out2(WE2), .out3(WE3), .out4(WE4), .out5(WE5), .out6(WE6), .out7(WE7),
    .out8(WE8), .out9(WE9), .out10(WE10), .out11(WE11), .out12(WE12), .out13(WE13), .out14(WE14),
    .out15(WE15), .out16(WE16), .out17(WE17), .out18(WE18), .out19(WE19), .out20(WE20), .out21(WE21),
    .out22(WE22), .out23(WE23), .out24(WE24), .out25(WE25), .out26(WE26), .out27(WE27), .out28(WE28),
    .out29(WE29), .out30(WE30), .out31(WE31), .in(RegWrite), .sel(RegC_write));
  Multiplexer #(.select(5), .width(32)) multiplexer_1 (
    .in0(Reg0_out), .in1(Reg1_out), .in2(Reg2_out), .in3(Reg3_out), .in4(Reg4_out), .in5(Reg5_out),
    .in6(Reg6_out), .in7(Reg7_out), .in8(Reg8_out), .in9(Reg9_out), .in10(Reg10_out), .in11(Reg11_out),
    .in12(Reg12_out), .in13(Reg13_out), .in14(Reg14_out), .in15(Reg15_out), .in16(Reg16_out),
    .in17(Reg17_out), .in18(Reg18_out), .in19(Reg19_out), .in20(Reg20_out), .in21(Reg21_out),
    .in22(Reg22_out), .in23(Reg23_out), .in24(Reg24_out), .in25(Reg25_out), .in26(Reg26_out),
    .in27(Reg27_out), .in28(Reg28_out), .in29(Reg29_out), .in30(Reg30_out), .in31(Reg31_out),
    .out(RegA_Data), .sel(RegA_read));
  Register #(.width(32)) Reg0 (.D({32{1'b0}}), .en(WE0), .clk(CLK), .Q(Reg0_out));  // open: clr
  Register #(.width(32)) Reg1 (.D(RegC_Data), .en(WE1), .clk(CLK), .Q(Reg1_out));  // open: clr
  Register #(.width(32)) Reg2 (.D(RegC_Data), .en(WE2), .clk(CLK), .Q(Reg2_out));  // open: clr
  Register #(.width(32)) Reg3 (.D(RegC_Data), .en(WE3), .clk(CLK), .Q(Reg3_out));  // open: clr
  Register #(.width(32)) Reg4 (.D(RegC_Data), .en(WE4), .clk(CLK), .Q(Reg4_out));  // open: clr
  Register #(.width(32)) Reg5 (.D(RegC_Data), .en(WE5), .clk(CLK), .Q(Reg5_out));  // open: clr
  Register #(.width(32)) Reg6 (.D(RegC_Data), .en(WE6), .clk(CLK), .Q(Reg6_out));  // open: clr
  Register #(.width(32)) Reg7 (.D(RegC_Data), .en(WE7), .clk(CLK), .Q(Reg7_out));  // open: clr
  Register #(.width(32)) Reg8 (.D(RegC_Data), .en(WE8), .clk(CLK), .Q(Reg8_out));  // open: clr
  Register #(.width(32)) Reg9 (.D(RegC_Data), .en(WE9), .clk(CLK), .Q(Reg9_out));  // open: clr
  Register #(.width(32)) Reg10 (.D(RegC_Data), .en(WE10), .clk(CLK), .Q(Reg10_out));  // open: clr
  Register #(.width(32)) Reg11 (.D(RegC_Data), .en(WE11), .clk(CLK), .Q(Reg11_out));  // open: clr
  Register #(.width(32)) Reg12 (.D(RegC_Data), .en(WE12), .clk(CLK), .Q(Reg12_out));  // open: clr
  Register #(.width(32)) Reg13 (.D(RegC_Data), .en(WE13), .clk(CLK), .Q(Reg13_out));  // open: clr
  Register #(.width(32)) Reg14 (.D(RegC_Data), .en(WE14), .clk(CLK), .Q(Reg14_out));  // open: clr
  Register #(.width(32)) Reg15 (.D(RegC_Data), .en(WE15), .clk(CLK), .Q(Reg15_out));  // open: clr
  Register #(.width(32)) Reg16 (.D(RegC_Data), .en(WE16), .clk(CLK), .Q(Reg16_out));  // open: clr
  Register #(.width(32)) Reg17 (.D(RegC_Data), .en(WE17), .clk(CLK), .Q(Reg17_out));  // open: clr
  Register #(.width(32)) Reg18 (.D(RegC_Data), .en(WE18), .clk(CLK), .Q(Reg18_out));  // open: clr
  Register #(.width(32)) Reg19 (.D(RegC_Data), .en(WE19), .clk(CLK), .Q(Reg19_out));  // open: clr
  Register #(.width(32)) Reg20 (.D(RegC_Data), .en(WE20), .clk(CLK), .Q(Reg20_out));  // open: clr
  Register #(.width(32)) Reg21 (.D(RegC_Data), .en(WE21), .clk(CLK), .Q(Reg21_out));  // open: clr
  Register #(.width(32)) Reg22 (.D(RegC_Data), .en(WE22), .clk(CLK), .Q(Reg22_out));  // open: clr
  Register #(.width(32)) Reg23 (.D(RegC_Data), .en(WE23), .clk(CLK), .Q(Reg23_out));  // open: clr
  Multiplexer #(.select(5), .width(32)) multiplexer_2 (
    .in0(Reg0_out), .in1(Reg1_out), .in2(Reg2_out), .in3(Reg3_out), .in4(Reg4_out), .in5(Reg5_out),
    .in6(Reg6_out), .in7(Reg7_out), .in8(Reg8_out), .in9(Reg9_out), .in10(Reg10_out), .in11(Reg11_out),
    .in12(Reg12_out), .in13(Reg13_out), .in14(Reg14_out), .in15(Reg15_out), .in16(Reg16_out),
    .in17(Reg17_out), .in18(Reg18_out), .in19(Reg19_out), .in20(Reg20_out), .in21(Reg21_out),
    .in22(Reg22_out), .in23(Reg23_out), .in24(Reg24_out), .in25(Reg25_out), .in26(Reg26_out),
    .in27(Reg27_out), .in28(Reg28_out), .in29(Reg29_out), .in30(Reg30_out), .in31(Reg31_out),
    .out(RegB_Data), .sel(RegB_read));
  Register #(.width(32)) Reg24 (.D(RegC_Data), .en(WE24), .clk(CLK), .Q(Reg24_out));  // open: clr
  Register #(.width(32)) Reg25 (.D(RegC_Data), .en(WE25), .clk(CLK), .Q(Reg25_out));  // open: clr
  Register #(.width(32)) Reg26 (.D(RegC_Data), .en(WE26), .clk(CLK), .Q(Reg26_out));  // open: clr
  Register #(.width(32)) Reg27 (.D(RegC_Data), .en(WE27), .clk(CLK), .Q(Reg27_out));  // open: clr
  Register #(.width(32)) Reg28 (.D(RegC_Data), .en(WE28), .clk(CLK), .Q(Reg28_out));  // open: clr
  Register #(.width(32)) Reg29 (.D(RegC_Data), .en(WE29), .clk(CLK), .Q(Reg29_out));  // open: clr
  Register #(.width(32)) Reg30 (.D(RegC_Data), .en(WE30), .clk(CLK), .Q(Reg30_out));  // open: clr
  Register #(.width(32)) Reg31 (.D(RegC_Data), .en(WE31), .clk(CLK), .Q(Reg31_out));  // open: clr

  // Other names for the same wires on the sheet: RegC_writingData[31:0] = RegC_Data
endmodule

module MemInstructions (
  input  [11:0] PC,
  output [31:0] Instruction
);

  ROM #(.addrWidth(12), .dataWidth(32)) rom_1 (.addr(PC), .data(Instruction));

  // Notes on the sheet:
  //   contents of rom_1 (hex, n*v repeats v):
  //   2008000a 2409ffff 3c0a1234 354a5678 310b000f 390c000f 1086820 1087021 1087822 1088023 1098824
  //   1099025 1099826 109a027 8a880 8b042 9b843 108c004 108c806 109d007 128d82a 128e02b 291d0064 2d3e0064
  //   ac0a0000 a40a0004 a00a0006 8c1f0000 84010004 94020004 80030006 90040006 11080001 800002d 15090001
  //   800002d 19200001 800002d 1d000001 800002d 5200001 800002d 5010001 800002d 800002e 800002d 800002e
endmodule

module ProgramCounter (
  input  [31:0] Imm32,
  input  RESET,
  input  JUMP,
  input  BRANCH,
  output [31:0] PC
);

  wire clock_1_out;
  wire [31:0] adder_1_out, adder_2_out, Imm32_t, multiplexer_1_out;

  Multiplexer #(.select(2), .width(32)) multiplexer_1 (
    .in0(adder_2_out), .in1(adder_1_out), .in2(Imm32_t), .in3({32{1'b0}}), .out(multiplexer_1_out),
    .sel({JUMP, BRANCH}));
  Register #(.width(32)) register_1 (.D(multiplexer_1_out), .clk(clock_1_out), .Q(PC), .clr(RESET));  // open: en
  Clock clock_1 (.out(clock_1_out));
  Shifter #(.width(32)) shifter_1 (.in(Imm32), .\dist (5'b00010), .out(Imm32_t));
  Adder #(.width(32)) adder_1 (.a(Imm32_t), .b(adder_2_out), .out(adder_1_out));  // open: cin, cout
  Adder #(.width(32)) adder_2 (.a(32'h4), .b(PC), .out(adder_2_out));  // open: cin, cout
endmodule

module BranchUnit (
  input  negativeFlag,
  input  zeroFlag,
  input  BEQ,
  input  BNE,
  input  BLTZ,
  input  BLEZ,
  input  BGTZ,
  input  BGEZ,
  output BRANCH
);

  wire and_1_out, and_2_out, and_3_out, and_4_out, and_5_out, and_6_out, not_1_out, not_2_out, not_3_out,
       or_1_out;

  not not_1 (not_1_out, zeroFlag);
  not not_2 (not_2_out, negativeFlag);
  not not_3 (not_3_out, zeroFlag);
  or or_1 (or_1_out, negativeFlag, zeroFlag);
  and and_1 (and_1_out, BEQ, zeroFlag);
  and and_2 (and_2_out, not_3_out, BNE);
  and and_3 (and_3_out, BLTZ, negativeFlag);
  and and_4 (and_4_out, BGTZ, not_1_out, not_2_out);
  and and_5 (and_5_out, BLEZ, or_1_out);
  and and_6 (and_6_out, BGEZ, not_2_out);
  or or_2 (BRANCH, and_1_out, and_2_out, and_3_out, and_5_out, and_4_out, and_6_out);
endmodule

module ControlUnit (
  input  [5:0] Opcode,
  input  [4:0] Rs,
  input  [4:0] Rt,
  input  [4:0] Rd,
  input  [4:0] sa,
  input  [5:0] func,
  input  [15:0] imm16,
  input  [25:0] imm26,
  output [4:0] RA,
  output [4:0] RB,
  output [4:0] RC,
  output [31:0] Imm32,
  output SLTtype,
  output MemtoReg,
  output ALUsrc,
  output MemRead,
  output RegWrite,
  output MemWrite,
  output [1:0] MemWriteSize,
  output [2:0] MemReadType,
  output [3:0] ALUcontrol,
  output JUMP,
  output [1:0] ShiftControl,
  output BEQ,
  output BNE,
  output BLEZ,
  output BGTZ,
  output BLTZ,
  output BGEZ
);

  wire add, addi, addiu, addu, and_1_out, and_2_out, and_3_out, and_4_out, and_5_out, and_11_out, and_12_out,
       and_13_out, and_14_out, and_15_out, and_22_out, and_23_out, and_24_out, and_25_out, and_26_out,
       and_27_out, and_47_out, and_48_out, andi, andR, lb, lbu, lh, lhu, norR, ori, orR, R_type, sb, sh,
       sllR, sllvR, slti, sltiu, sltR, sltuR, sraR, sravR, srlR, srlvR, sub, subu, sw, xori, xorR, zeroExtend;
  wire [31:0] bit_extender_1_out, bit_extender_2_out, bit_extender_3_out, multiplexer_2_out;

  and and_1 (and_1_out, ~func[0], ~func[1], ~func[2], ~func[3], ~func[4], func[5]);  // AND_Gate
  and and_2 (and_2_out, ~func[0], func[1], ~func[2], ~func[3], ~func[4], func[5]);  // AND_Gate
  and and_3 (and_3_out, func[0], func[1], ~func[2], ~func[3], ~func[4], func[5]);  // AND_Gate
  and and_4 (and_4_out, ~func[0], func[1], ~func[2], func[3], ~func[4], func[5]);  // AND_Gate
  and and_5 (and_5_out, func[0], ~func[1], ~func[2], ~func[3], ~func[4], func[5]);  // AND_Gate
  and and_6 (add, R_type, and_1_out);
  and and_7 (addu, R_type, and_5_out);
  and and_8 (sub, R_type, and_2_out);
  and and_9 (subu, R_type, and_3_out);
  and and_10 (sltR, R_type, and_4_out);
  Multiplexer #(.width(5)) multiplexer_1 (.in0(Rt), .in1(Rd), .out(RC), .sel(R_type));
  and and_11 (and_11_out, ~func[0], ~func[1], func[2], ~func[3], ~func[4], func[5]);  // AND_Gate
  and and_12 (and_12_out, func[0], ~func[1], func[2], ~func[3], ~func[4], func[5]);  // AND_Gate
  and and_13 (and_13_out, ~func[0], func[1], func[2], ~func[3], ~func[4], func[5]);  // AND_Gate
  and and_14 (and_14_out, func[0], func[1], func[2], ~func[3], ~func[4], func[5]);  // AND_Gate
  and and_15 (and_15_out, func[0], func[1], ~func[2], func[3], ~func[4], func[5]);  // AND_Gate
  and and_16 (R_type, ~Opcode[0], ~Opcode[1], ~Opcode[2], ~Opcode[3], ~Opcode[4], ~Opcode[5]);  // AND_Gate
  and and_17 (andR, R_type, and_11_out);
  and and_18 (orR, R_type, and_12_out);
  and and_19 (xorR, R_type, and_13_out);
  and and_20 (norR, R_type, and_14_out);
  and and_21 (sltuR, R_type, and_15_out);
  assign bit_extender_1_out = {{16{imm16[15]}}, imm16};  // Bit_Extender bit_extender_1
  assign bit_extender_2_out = {{16{1'b0}}, imm16};  // Bit_Extender bit_extender_2
  Multiplexer #(.width(32)) multiplexer_2 (
    .in0(bit_extender_1_out), .in1(bit_extender_2_out), .out(multiplexer_2_out), .sel(zeroExtend));
  assign bit_extender_3_out = {{6{1'b0}}, imm26};  // Bit_Extender bit_extender_3
  and and_22 (and_22_out, ~func[0], ~func[1], ~func[2], ~func[3], ~func[4], ~func[5]);  // AND_Gate
  and and_23 (and_23_out, ~func[0], func[1], ~func[2], ~func[3], ~func[4], ~func[5]);  // AND_Gate
  and and_24 (and_24_out, func[0], func[1], ~func[2], ~func[3], ~func[4], ~func[5]);  // AND_Gate
  and and_25 (and_25_out, ~func[0], ~func[1], func[2], ~func[3], ~func[4], ~func[5]);  // AND_Gate
  and and_26 (and_26_out, ~func[0], func[1], func[2], ~func[3], ~func[4], ~func[5]);  // AND_Gate
  and and_27 (and_27_out, func[0], func[1], func[2], ~func[3], ~func[4], ~func[5]);  // AND_Gate
  Multiplexer #(.width(32)) multiplexer_3 (.in0(multiplexer_2_out), .in1(bit_extender_3_out), .out(Imm32), .sel(JUMP));
  nor nor_1 (ALUsrc, R_type, BEQ, BNE, BLEZ, BGTZ, BLTZ, BGEZ);
  and and_28 (sllR, R_type, and_22_out);
  and and_29 (srlR, R_type, and_23_out);
  and and_30 (sraR, R_type, and_24_out);
  and and_31 (sllvR, R_type, and_25_out);
  and and_32 (srlvR, R_type, and_26_out);
  and and_33 (sravR, R_type, and_27_out);
  or or_1 (zeroExtend, xori, ori, andi);
  or or_2 (SLTtype, sltuR, sltiu);
  nor nor_2 (RegWrite, BEQ, BLEZ, BGTZ, BLTZ, BGEZ, JUMP, sb, sh, sw, BNE);
  and and_34 (addi, ~Opcode[0], ~Opcode[1], ~Opcode[2], Opcode[3], ~Opcode[4], ~Opcode[5]);  // AND_Gate
  and and_35 (addiu, Opcode[0], ~Opcode[1], ~Opcode[2], Opcode[3], ~Opcode[4], ~Opcode[5]);  // AND_Gate
  and and_36 (andi, ~Opcode[0], ~Opcode[1], Opcode[2], Opcode[3], ~Opcode[4], ~Opcode[5]);  // AND_Gate
  and and_37 (ori, Opcode[0], ~Opcode[1], Opcode[2], Opcode[3], ~Opcode[4], ~Opcode[5]);  // AND_Gate
  and and_38 (xori, ~Opcode[0], Opcode[1], Opcode[2], Opcode[3], ~Opcode[4], ~Opcode[5]);  // AND_Gate
  and and_39 (ShiftControl[1], Opcode[0], Opcode[1], Opcode[2], Opcode[3], ~Opcode[4], ~Opcode[5]);  // AND_Gate
  and and_40 (slti, ~Opcode[0], Opcode[1], ~Opcode[2], Opcode[3], ~Opcode[4], ~Opcode[5]);  // AND_Gate
  and and_41 (sltiu, Opcode[0], Opcode[1], ~Opcode[2], Opcode[3], ~Opcode[4], ~Opcode[5]);  // AND_Gate
  or or_3 (ALUcontrol[3], srlR, sraR, srlvR, sravR);
  or or_4 (MemRead, lb, lh, MemReadType[2], lbu, lhu);
  or or_5 (MemWrite, sb, sh, sw);
  and and_42 (JUMP, ~Opcode[0], Opcode[1], ~Opcode[2], ~Opcode[3], ~Opcode[4], ~Opcode[5]);  // AND_Gate
  and and_43 (BEQ, ~Opcode[0], ~Opcode[1], Opcode[2], ~Opcode[3], ~Opcode[4], ~Opcode[5]);  // AND_Gate
  and and_44 (BNE, Opcode[0], ~Opcode[1], Opcode[2], ~Opcode[3], ~Opcode[4], ~Opcode[5]);  // AND_Gate
  and and_45 (BLEZ, ~Opcode[0], Opcode[1], Opcode[2], ~Opcode[3], ~Opcode[4], ~Opcode[5]);  // AND_Gate
  and and_46 (BGTZ, Opcode[0], Opcode[1], Opcode[2], ~Opcode[3], ~Opcode[4], ~Opcode[5]);  // AND_Gate
  and and_47 (and_47_out, Opcode[0], ~Opcode[1], ~Opcode[2], ~Opcode[3], ~Opcode[4], ~Opcode[5]);  // AND_Gate
  and and_48 (and_48_out, Opcode[0], ~Opcode[1], ~Opcode[2], ~Opcode[3], ~Opcode[4], ~Opcode[5]);  // AND_Gate
  and and_49 (BGEZ, and_48_out, Rt[0]);
  and and_50 (BLTZ, and_47_out, ~Rt[0]);  // AND_Gate
  or or_6 (ALUcontrol[2], xorR, norR, sltR, sltuR, ShiftControl[1], slti, sltiu, sllvR, sllR, xori);
  or or_7 (MemWriteSize[1], sh, sw);
  or or_8 (MemWriteSize[0], sb, sw);
  and and_51 (lb, ~Opcode[0], ~Opcode[1], ~Opcode[2], ~Opcode[3], ~Opcode[4], Opcode[5]);  // AND_Gate
  and and_52 (lh, Opcode[0], ~Opcode[1], ~Opcode[2], ~Opcode[3], ~Opcode[4], Opcode[5]);  // AND_Gate
  and and_53 (MemReadType[2], Opcode[0], Opcode[1], ~Opcode[2], ~Opcode[3], ~Opcode[4], Opcode[5]);  // AND_Gate
  and and_54 (lbu, ~Opcode[0], ~Opcode[1], Opcode[2], ~Opcode[3], ~Opcode[4], Opcode[5]);  // AND_Gate
  and and_55 (lhu, Opcode[0], ~Opcode[1], Opcode[2], ~Opcode[3], ~Opcode[4], Opcode[5]);  // AND_Gate
  and and_56 (sb, ~Opcode[0], ~Opcode[1], ~Opcode[2], Opcode[3], ~Opcode[4], Opcode[5]);  // AND_Gate
  and and_57 (sh, Opcode[0], ~Opcode[1], ~Opcode[2], Opcode[3], ~Opcode[4], Opcode[5]);  // AND_Gate
  and and_58 (sw, Opcode[0], Opcode[1], ~Opcode[2], Opcode[3], ~Opcode[4], Opcode[5]);  // AND_Gate
  or or_9 (MemReadType[0], lbu, lhu);
  or or_10 (MemReadType[1], lhu, lh);
  or or_11 (ALUcontrol[1], ShiftControl[1], andR, andi, orR, sllR, sllvR, ori, xorR, xori);
  or or_12 (ShiftControl[0], sllvR, srlvR, sravR);
  or or_13 (ALUcontrol[0], sltuR, sllR, sub, orR, sltR, subu, ori, sltiu, ShiftControl[1], sraR, sllvR, sravR, BNE, BEQ, BLEZ, BLTZ, BGTZ, BGEZ, slti);

  assign MemtoReg = MemRead;
  assign RA = Rs;
  assign RB = Rt;

  // Other names for the same wires on the sheet: S0 = ALUcontrol[0]; S1 = ALUcontrol[1]; S2 = ALUcontrol[2];
  //   S3 = ALUcontrol[3]; W0 = MemReadType[0]; W1 = MemReadType[1]; lw = MemReadType[2]; W2 = MemReadType[2];
  //   R0 = MemWriteSize[0]; R1 = MemWriteSize[1]; RegDst[4:0] = RC; lui = ShiftControl[1]
endmodule

module MemData (
  input  [31:0] StoreData,
  input  [1:0] offset,
  input  [23:0] RAMaddress,
  input  MemWrite,
  input  MemRead,
  input  CLK,
  input  [1:0] MemWriteSize,
  input  [2:0] MemReadType,
  output [31:0] LoadData
);

  wire [3:0] decoder_1_out0, multiplexer_1_out, multiplexer_2_out;
  wire [7:0] multiplexer_4_out;
  wire [15:0] multiplexer_5_out;
  wire [31:0] bit_extender_1_out, bit_extender_2_out, bit_extender_3_out, bit_extender_4_out, MemData,
       multiplexer_3_out;

  Decoder #(.enable("false"), .select(2)) decoder_1 (
    .out0(decoder_1_out0[0]), .out1(decoder_1_out0[1]), .out2(decoder_1_out0[2]), .out3(decoder_1_out0[3]),
    .sel(offset));
  Multiplexer #(.width(4)) multiplexer_1 (.in0(4'b0011), .in1(4'b1100), .out(multiplexer_1_out), .sel(offset[1]));
  Multiplexer #(.select(2), .width(4)) multiplexer_2 (
    .in0(4'b0000), .in1(decoder_1_out0), .in2(multiplexer_1_out), .in3(4'b1111), .out(multiplexer_2_out),
    .sel(MemWriteSize));
  Multiplexer #(.select(2), .width(32)) multiplexer_3 (
    .in0({32{1'b0}}), .in1({StoreData[7:0], StoreData[7:0], StoreData[7:0], StoreData[7:0]}),
    .in2({StoreData[15:0], StoreData[15:0]}), .in3(StoreData), .out(multiplexer_3_out), .sel(MemWriteSize));
  RAM #(.addrWidth(24), .asyncread("true"), .byteenables("byteEnables"), .dataWidth(32)) ram_1 (
    .addr(RAMaddress), .we(MemWrite), .oe(MemRead), .clk(CLK), .din(multiplexer_3_out), .dout(MemData),
    .be3(multiplexer_2_out[3]), .be2(multiplexer_2_out[2]), .be1(multiplexer_2_out[1]),
    .be0(multiplexer_2_out[0]));
  Multiplexer #(.select(2), .width(8)) multiplexer_4 (
    .in0(MemData[7:0]), .in1(MemData[15:8]), .in2(MemData[23:16]), .in3(MemData[31:24]),
    .out(multiplexer_4_out), .sel(offset));
  Multiplexer #(.width(16)) multiplexer_5 (
    .in0(MemData[15:0]), .in1(MemData[31:16]), .out(multiplexer_5_out), .sel(offset[1]));
  assign bit_extender_1_out = {{24{multiplexer_4_out[7]}}, multiplexer_4_out};  // Bit_Extender bit_extender_1
  assign bit_extender_2_out = {{24{1'b0}}, multiplexer_4_out};  // Bit_Extender bit_extender_2
  assign bit_extender_3_out = {{16{multiplexer_5_out[15]}}, multiplexer_5_out};  // Bit_Extender bit_extender_3
  assign bit_extender_4_out = {{16{1'b0}}, multiplexer_5_out};  // Bit_Extender bit_extender_4
  Multiplexer #(.select(3), .width(32)) multiplexer_6 (
    .in0(bit_extender_1_out), .in1(bit_extender_2_out), .in2(bit_extender_3_out), .in3(bit_extender_4_out),
    .in4(MemData), .out(LoadData), .sel(MemReadType));  // open: in5, in6, in7

  // Other names for the same wires on the sheet: offsetHalf = offset[1]

  // Notes on the sheet:
  //   sb: 01, sh: 10, sw: 11
  //   lb:000, lbu:001, lh:010, lhu:011, lw:100
endmodule
